# Fritzing sketch AMCur-1CH (saved by Fritzing 0.9.3b)

parts:
  Bauteil1 = Arduino Pro Mini (3.3V)
  LCD_Backlight = Momentary Switch [package=ksa_sealed_tac_switch]
  LED = LED - 3mm [color="Green (560nm)" package="3 mm [THT]"]
  R1+R2 = Resistor [tolerance=±5% resistance=330 package=THT]
  U1 = CC1101 [part_number=CC1101]
  R2 = Resistor [tolerance=±5% resistance=330 package=THT]
  LED_(BUSY) = LED - 3mm [color="Red (635nm)" package="3 mm [THT]"]
  0x4B = ADS1115 16-bit ADC Breakout
  0x27 = LCM1602 IIC [part_number="LCM1602 IIC" chip_label="LCM1602 IIC" package="DIP (Dual Inline) [THT]"]
  Bauteil2 = Standard LCD 16x2 white on blue [part_number=181]  # not connected
  L1 = sct-013 [part_number=sct-013 package="4Ucon 08780 [THT]"]
  Config = Momentary Switch [package=ksa_sealed_tac_switch]
  5V = Power plug

nets:
  N1: Bauteil1.A4, 0x4B.SDA, 0x27.SDA
  N2: Bauteil1.A5, 0x4B.SCL, 0x4B.ADDR, 0x27.SCL
  VCC: Bauteil1.RAW, 0x27.VCC, 5V.VCC
  GND: Bauteil1.GND, LED.cathode, U1.2, 0x4B.GND, 0x27.GND, 5V.GND
  VCC_2: Bauteil1.VCC, U1.1, 0x4B.VDD
  N3: Bauteil1.SCK, U1.4
  N4: Bauteil1.MISO, U1.5
  N5: Bauteil1.MOSI, U1.3
  N6: Bauteil1.D10, U1.8
  N7: Bauteil1.D8, Config.3
  N8: Bauteil1.D6, LCD_Backlight.2
  N9: Bauteil1.D5, R2.Pin_0
  N10: Bauteil1.D4, R1+R2.Pin_0
  N11: Bauteil1.D2, U1.7
  N12: LCD_Backlight.3, LED_(BUSY).cathode, Config.2
  N13: LED.anode, R1+R2.Pin_1
  N14: R2.Pin_1, LED_(BUSY).anode
  N15: 0x4B.A0, L1.pin_0
  N16: 0x4B.A1, L1.pin_1

custom parts:
  ADS1115 16-bit ADC Breakout: ADS1015 12-bit I2C ADC+PGA Breakout
  LCM1602 IIC: I2C-Module to use a 1602 or 2004 LCD on with the wire.h libory Serial LCD Modul
  Standard LCD 16x2 white on blue: Standard HD44780 LCDs are useful for creating standalone projects. * 16 characters wide, 2 rows * White text on blue background * Connection port is 0.1" pitch, single row for easy breadboarding and wiring
  sct-013: sct-013 Current transformer. The pcb footprint is from the 3.5mm stereo jack (as the sensor comes with a 3.5 mm stero plug).
